# Fritzing sketch kegerator (saved by Fritzing 0.9.2b)
breadboards: 1

parts:
  U1 = ESP8266 WiFi Module [part_number=ESP8266]
  3_3V_Serial_Module_-_FTDI = FTDI Basic Programmer
  U2 = Voltage Regulator - 3.3V [package="TO220 [THT]"]
  Flow1 = Infrared Proximity Sensor
  Flow2 = Infrared Proximity Sensor
  R1 = Resistor [tolerance=±5% resistance=1k package=THT]
  S1 = Pushbutton [part_number="Serial Boot" package=THT]
  LED1 = RGB LED - (4 legs) [package="5 mm [THT]"]
  R2 = Resistor [tolerance=±20% resistance=1k package=THT]  # not connected

nets:
  N1: U1.RXD, 3_3V_Serial_Module_-_FTDI.TXO
  VCC: U1.VCC, U1.GPIO_2, U1.CH_PD, 3_3V_Serial_Module_-_FTDI.POWER, U2.output_voltage, Flow1.Vcc, Flow2.Vcc, R1.Pin_1
  N2: U1.GPIO_0, S1.leg1
  N3: U1.GPIO_16, LED1.blue_cathode
  GND: U1.GND, U2.GND, Flow1.GND, Flow2.GND, LED1.common_anode
  N4: U1.TXD, 3_3V_Serial_Module_-_FTDI.RXI
  N5: U1.GPIO_12, LED1.green_cathode
  N6: U1.GPIO_13, Flow2.Vout
  N7: U1.GPIO_14, Flow1.Vout
  N8: U1.GPIO_15, LED1.red_cathode

notes:
  GPIO_15 needs to be pulled low to boot, GPI_0 is high to boot from flash, low to boot from serial (upload code), GPIO_2 needs to be high at boot

custom parts:
  ESP8266 WiFi Module: Generic WiFi Module based on the ESP8266 with onboard PCB antenna and UART communications
